// Logisim project lab1.6.circ as structural Verilog: 2 circuits, main circuit 4-1MUX
module _4_1MUX (
  input  [3:0] INPUT,
  input  [1:0] SELECT,
  output OUTPUT
);

  wire n2_1mux_1_y, n2_1mux_3_y;

  _2_1MUX u_2_1mux_1 (.D0(INPUT[0]), .D1(INPUT[1]), .S(SELECT[0]), .Y(n2_1mux_1_y));
  _2_1MUX u_2_1mux_2 (.D0(n2_1mux_1_y), .D1(n2_1mux_3_y), .S(SELECT[1]), .Y(OUTPUT));
  _2_1MUX u_2_1mux_3 (.D0(INPUT[2]), .D1(INPUT[3]), .S(SELECT[0]), .Y(n2_1mux_3_y));

  // Other names for the same wires on the sheet: DATA[3:0] = INPUT; S[1:0] = SELECT; Y = OUTPUT
endmodule

module _2_1MUX (
  input  D0,
  input  D1,
  input  S,
  output Y
);

  wire transistor_1_out;

  Transistor transistor_1 (.in(1'b1), .out(transistor_1_out), .gate(S));
  Transistor #(.\type ("n")) transistor_2 (.in(1'b0), .out(transistor_1_out), .gate(S));
  // Transmission_Gate transmission_1: pin names not known; wires that end beside it: D0, D0, S, transistor_1_out, Y
  // Transmission_Gate transmission_2: pin names not known; wires that end beside it: 1'b0, D1, transistor_1_out, S, Y

  // Notes on the sheet:
  //   输入引脚
  //   请勿修改引脚名称及电路封装外观
  //   提示：使用传输门和晶体管来实现二选一多路选择器，禁止直接使用选择器组件。
  //   输出引脚
endmodule
