// Logisim project 思考题1.circ as structural Verilog: 1 circuit, main circuit main
module main (
  input  D0,
  input  D1,
  input  S,
  output Y
);

  wire nand_1_out, nand_2_out, nand_3_out;

  nand nand_1 (nand_1_out, D0, nand_3_out);
  nand nand_2 (nand_2_out, D1, S);
  nand nand_3 (nand_3_out, S, S);
  nand nand_4 (Y, nand_1_out, nand_2_out);

  // Notes on the sheet:
  //   输入引脚
  //   请勿修改引脚名称及电路封装外观
  //   提示：使用独立逻辑门实现二选一多路选择器，禁止直接使用选择器组件。
  //   输出引脚
endmodule
