// Logisim project 思考题3.circ as structural Verilog: 1 circuit, main circuit main
module main (
  input  in_1,
  input  in_2,
  input  in_3,
  input  in_4,
  output p
);

  wire xor_1_out, xor_2_out, xor_3_out;

  xor xor_1 (xor_1_out, in_1, in_2);
  xor xor_2 (xor_2_out, in_3, in_4);
  xor xor_3 (xor_3_out, xor_1_out, xor_2_out);
  not not_1 (p, xor_3_out);

  // Other names for the same wires on the sheet: D0 = in_1; D1 = in_2; D2 = in_3; D3 = in_4
endmodule
