// Logisim project 无符号比较.circ as structural Verilog: 1 circuit, main circuit main
module main (
  input  [3:0] X,
  input  [3:0] Y,
  input  [3:0] X_2,
  input  [3:0] Y_2,
  output \X与Y是否相等_无符号 ,
  output \X是否大于Y_无符号 
);

  wire and_1_out, and_2_out, and_3_out, and_4_out, xnor_1_out, xnor_2_out, xnor_3_out, xnor_4_out,
       xnor_5_out, xnor_6_out, xnor_7_out;

  xnor xnor_1 (xnor_1_out, X_2[3], Y_2[3]);
  xnor xnor_2 (xnor_2_out, X_2[2], Y_2[2]);
  xnor xnor_3 (xnor_3_out, X_2[1], Y_2[1]);
  xnor xnor_4 (xnor_4_out, X[0], Y[0]);
  xnor xnor_5 (xnor_5_out, X[1], Y[1]);
  xnor xnor_6 (xnor_6_out, X[2], Y[2]);
  xnor xnor_7 (xnor_7_out, X[3], Y[3]);
  and and_1 (and_1_out, X_2[3], ~Y_2[3]);  // AND_Gate
  and and_2 (and_2_out, xnor_1_out, X_2[2], ~Y_2[2]);  // AND_Gate
  and and_3 (and_3_out, xnor_1_out, xnor_2_out, X_2[1], ~Y_2[1]);  // AND_Gate
  and and_4 (and_4_out, xnor_1_out, xnor_2_out, xnor_3_out, X_2[0], ~Y_2[0]);  // AND_Gate
  and and_5 (\X与Y是否相等_无符号 , xnor_4_out, xnor_5_out, xnor_6_out, xnor_7_out);
  or or_1 (\X是否大于Y_无符号 , and_1_out, and_2_out, and_3_out, and_4_out);
endmodule
