// Logisim project 思考2.circ as structural Verilog: 1 circuit, main circuit CNTR4U
module CNTR4U (
  input  CLK,
  input  LD,
  input  CLR,
  input  D0,
  input  D1,
  input  D2,
  input  D3,
  input  ENP,
  input  ENT,
  output Q0,
  output Q1,
  output Q2,
  output Q3,
  output RCO
);

  wire and_1_out, and_2_out, and_3_out, and_4_out, and_5_out, and_6_out, and_7_out, and_8_out, and_9_out,
       and_10_out, and_11_out, and_12_out, and_13_out, and_14_out, d_ff_1_qn, d_ff_2_qn, d_ff_3_qn,
       d_ff_4_qn, nor_1_out, nor_2_out, not_1_out, not_2_out, not_3_out, not_4_out, not_5_out, not_6_out,
       not_7_out, not_8_out, not_9_out, or_1_out, or_2_out, or_3_out, or_4_out, or_5_out, tunnel, xor_1_out,
       xor_2_out, xor_3_out, xor_4_out;

  not not_1 (not_1_out, CLK);
  not not_2 (not_2_out, or_1_out);
  or or_1 (or_1_out, tunnel, CLR);
  not not_3 (not_3_out, d_ff_1_qn);
  nor nor_1 (nor_1_out, d_ff_1_qn, d_ff_2_qn);
  nor nor_2 (nor_2_out, d_ff_1_qn, d_ff_2_qn, d_ff_3_qn);
  and and_1 (and_1_out, ENP, ENT);
  not not_4 (not_4_out, ENT);
  and and_2 (and_2_out, LD, not_2_out);
  not not_5 (not_5_out, and_2_out);
  and and_3 (and_3_out, not_5_out, not_2_out);
  not not_6 (not_6_out, d_ff_1_qn);
  and and_4 (and_4_out, not_3_out, and_1_out);
  xor xor_1 (xor_1_out, and_4_out, not_7_out);
  not not_7 (not_7_out, d_ff_2_qn);
  and and_5 (and_5_out, nor_1_out, and_1_out);
  xor xor_2 (xor_2_out, and_5_out, not_8_out);
  not not_8 (not_8_out, d_ff_3_qn);
  and and_6 (and_6_out, nor_2_out, and_1_out);
  not not_9 (not_9_out, d_ff_4_qn);
  nor nor_3 (RCO, d_ff_4_qn, d_ff_1_qn, not_4_out, d_ff_2_qn, d_ff_3_qn);
  xor xor_3 (xor_3_out, and_1_out, not_6_out);
  xor xor_4 (xor_4_out, and_6_out, not_9_out);
  and and_7 (and_7_out, and_2_out, D0);
  and and_8 (and_8_out, and_3_out, xor_3_out);
  and and_9 (and_9_out, and_2_out, D1);
  and and_10 (and_10_out, and_3_out, xor_1_out);
  and and_11 (and_11_out, and_2_out, D2);
  and and_12 (and_12_out, and_3_out, xor_2_out);
  and and_13 (and_13_out, and_2_out, D3);
  and and_14 (and_14_out, and_3_out, xor_4_out);
  or or_2 (or_2_out, and_7_out, and_8_out);
  or or_3 (or_3_out, and_9_out, and_10_out);
  or or_4 (or_4_out, and_11_out, and_12_out);
  or or_5 (or_5_out, and_13_out, and_14_out);
  D_Flip_Flop #(.trigger("falling")) d_ff_1 (
    .clk(not_1_out), .D(or_2_out), .Q(Q0), .Qn(d_ff_1_qn));  // open: preset, reset
  D_Flip_Flop #(.trigger("falling")) d_ff_2 (
    .clk(not_1_out), .D(or_3_out), .Q(Q1), .Qn(d_ff_2_qn));  // open: preset, reset
  D_Flip_Flop #(.trigger("falling")) d_ff_3 (
    .clk(not_1_out), .D(or_4_out), .Q(Q2), .Qn(d_ff_3_qn));  // open: preset, reset
  D_Flip_Flop #(.trigger("falling")) d_ff_4 (
    .clk(not_1_out), .D(or_5_out), .Q(Q3), .Qn(d_ff_4_qn));  // open: preset, reset
  and and_15 (tunnel, Q0, ~Q1, ~Q2, Q3);  // AND_Gate

  // Notes on the sheet:
  //   输入引脚
  //   请勿修改引脚名称、电路名称及电路封装外观
  //   提示：使用独立逻辑门实现4位二进制同步计数器，禁止直接使用计数器组件。
  //   输出引脚
endmodule
