// Logisim project 思考题3.circ as structural Verilog
module main (
  input  in_1,
  input  in_2,
  input  in_3,
  input  in_4,
  input  in_5,
  input  [7:0] in_6,
  output [7:0] out_7
);

  wire tunnel;

  SHRG4U shrg4u_1 (
    .CLK(in_2), .CLR_L(in_1), .RIN(tunnel), .Q3(out_7[0]), .Q2(out_7[1]), .D3(in_6[0]), .D2(in_6[1]),
    .D1(in_6[2]), .Q1(out_7[2]), .Q0(out_7[3]), .D0(in_6[3]), .LIN(in_3), .S1(in_4), .S0(in_5));
  SHRG4U shrg4u_2 (
    .CLK(in_2), .CLR_L(in_1), .RIN(out_7[3]), .Q3(out_7[4]), .Q2(out_7[5]), .D3(in_6[4]), .D2(in_6[5]),
    .D1(in_6[6]), .Q1(out_7[6]), .Q0(out_7[7]), .D0(in_6[7]), .LIN(in_3), .S1(in_4), .S0(in_5));
  xor xor_1 (tunnel, out_7[0], out_7[7]);
endmodule
