// Logisim project lab4.3.circ as structural Verilog: 1 circuit, main circuit Adder32
// 加法器
module Adder32 (
  input  Cin,
  input  [31:0] X,
  input  [31:0] Y,
  output CF,
  output Cout,
  output OF,
  output SF,
  output [31:0] S,
  output ZF
);

  wire and_1_out, and_2_out, main_1_c16, nor_1_out, nor_2_out, nor_3_out, nor_4_out;
  wire [1:0] or_4_out, or_5_out, or_6_out, or_7_out;
  wire [7:0] or_2_out, or_3_out;

  lab4_2_main main_1 (.X(X[15:0]), .Y(Y[15:0]), .C0(Cin), .S(S[15:0]), .C16(main_1_c16));  // open: Pg, Gg
  lab4_2_main main_2 (.X(X[31:16]), .Y(Y[31:16]), .C0(main_1_c16), .S(S[31:16]), .C16(Cout));  // open: Pg, Gg
  xor xor_1 (CF, Cout, Cin);
  and and_1 (and_1_out, S[31], ~X[31], ~Y[31]);  // AND_Gate
  or or_1 (OF, and_1_out, and_2_out);
  and and_2 (and_2_out, ~S[31], X[31], Y[31]);  // AND_Gate
  assign or_2_out = S[7:0] | S[15:8];  // OR_Gate or_2, 8 bits wide
  assign or_3_out = S[23:16] | S[31:24];  // OR_Gate or_3, 8 bits wide
  // Probe on X
  // Probe on Y
  // Probe on S
  assign or_4_out = or_2_out[1:0] | or_2_out[3:2];  // OR_Gate or_4, 2 bits wide
  assign or_5_out = or_2_out[5:4] | or_2_out[7:6];  // OR_Gate or_5, 2 bits wide
  assign or_6_out = or_3_out[1:0] | or_3_out[3:2];  // OR_Gate or_6, 2 bits wide
  assign or_7_out = or_3_out[5:4] | or_3_out[7:6];  // OR_Gate or_7, 2 bits wide
  nor nor_1 (nor_1_out, or_4_out[0], or_4_out[1]);
  nor nor_2 (nor_2_out, or_5_out[0], or_5_out[1]);
  nor nor_3 (nor_3_out, or_6_out[0], or_6_out[1]);
  nor nor_4 (nor_4_out, or_7_out[0], or_7_out[1]);
  and and_3 (ZF, nor_1_out, nor_2_out, nor_3_out, nor_4_out);

  assign SF = S[31];

  // Notes on the sheet:
  //   Y: pull=down
  //   Cin: pull=down
  //   X: pull=down
  //   输入引脚区
  //   输出引脚区
  //   请勿修改引脚名称、电路名称及电路封装外观
  //   提示：使用16位并行加法器子电路实现32位快速加法器
  //   功能说明:32位Adder  S=X+Y，Cout为最高位进位位，Cin为进位输入， S为和，溢出OF、进位CF、零ZF、符号SF。
  //   +
  //   =
  //   无符号加法
endmodule
