// Logisim project 思考题1.circ as structural Verilog: 1 circuit, main circuit main
module main (
  input  [31:0] in_1,
  input  [31:0] in_2,
  input  [31:0] in_3,
  input  [31:0] in_4,
  input  in_5,
  output [31:0] out_6,
  output [31:0] out_7
);

  wire adder32_1_cout;

  Adder32 adder32_1 (.Cin(in_5), .Cout(adder32_1_cout), .X(in_1), .Y(in_3), .S(out_6));  // open: OF, CF, ZF, SF
  Adder32 adder32_2 (.Cin(adder32_1_cout), .X(in_2), .Y(in_4), .S(out_7));  // open: Cout, OF, CF, ZF, SF

  // Other names for the same wires on the sheet: cin = in_5; x0[31:0] = in_1; x1[31:0] = in_2; y0[31:0] = in_3;
  //   y1[31:0] = in_4; z0[31:0] = out_6; z1[31:0] = out_7
endmodule
