// Logisim project 思考题2-快速乘法器.circ as structural Verilog: 2 circuits, main circuit main
module main (
  input  [31:0] A,
  input  [31:0] B,
  output [31:0] out_3,
  output [31:0] out_4
);

  wire cell_1_ai_2, cell_1_bi_2, cell_1_cout, cell_2_ai_2, cell_2_bi_2, cell_2_cout, \cell_2_部分积1位输出 ,
       cell_3_ai_2, cell_3_bi_2, cell_3_cout, cell_4_bi_2, cell_4_cout, \cell_4_部分积1位输出 , \cell_5_部分积1位输出 ;

  CELL cell_1 (
    .CIN(1'b0), .Ai(A[0]), .Bi(B[0]), .\部分积1位输入 (1'b0), .\部分积1位输出 (out_3[0]), .cout(cell_1_cout),
    .Bi_2(cell_1_bi_2), .Ai_2(cell_1_ai_2));
  CELL cell_2 (
    .CIN(cell_1_cout), .Ai(A[1]), .Bi(cell_1_bi_2), .\部分积1位输入 (1'b0), .\部分积1位输出 (\cell_2_部分积1位输出 ),
    .cout(cell_2_cout), .Bi_2(cell_2_bi_2), .Ai_2(cell_2_ai_2));
  CELL cell_3 (
    .CIN(1'b0), .Ai(cell_1_ai_2), .Bi(B[1]), .\部分积1位输入 (\cell_2_部分积1位输出 ), .\部分积1位输出 (out_3[1]),
    .cout(cell_3_cout), .Bi_2(cell_3_bi_2), .Ai_2(cell_3_ai_2));
  CELL cell_4 (
    .CIN(cell_2_cout), .Ai(A[2]), .Bi(cell_2_bi_2), .\部分积1位输入 (1'b0), .\部分积1位输出 (\cell_4_部分积1位输出 ),
    .cout(cell_4_cout), .Bi_2(cell_4_bi_2));  // open: Ai_2
  CELL cell_5 (
    .CIN(cell_3_cout), .Ai(cell_2_ai_2), .Bi(cell_3_bi_2), .\部分积1位输入 (\cell_4_部分积1位输出 ),
    .\部分积1位输出 (\cell_5_部分积1位输出 ));  // open: cout, Bi_2, Ai_2
  CELL cell_6 (
    .CIN(1'b0), .Ai(cell_3_ai_2), .Bi(B[2]), .\部分积1位输入 (\cell_5_部分积1位输出 ), .\部分积1位输出 (out_3[2]));  // open: cout, Bi_2, Ai_2
  CELL cell_7 (.CIN(cell_4_cout), .Ai(A[3]), .Bi(cell_4_bi_2), .\部分积1位输入 (1'b0));  // open: 部分积1位输出, cout, Bi_2, Ai_2

  assign B[8] = B[9];

  // Other names for the same wires on the sheet: B7 = B[6]; B8 = B[7]; Z0 = out_3[0]; Z1 = out_3[1]; Z2 = out_3[2];
  //   Z3 = out_3[3]; Z4 = out_3[4]; Z5 = out_3[5]; Z6 = out_3[6]; Z7 = out_3[7]; Z8 = out_3[8]; Z9 = out_3[9];
  //   Z10 = out_3[10]; Z11 = out_3[11]; Z12 = out_3[12]; Z13 = out_3[13]; Z14 = out_3[14]; Z15 = out_3[15];
  //   Z16 = out_3[16]; Z17 = out_3[17]; Z18 = out_3[18]; Z19 = out_3[19]; Z20 = out_3[20]; Z21 = out_3[21];
  //   Z22 = out_3[22]; Z23 = out_3[23]; Z24 = out_3[24]; Z25 = out_3[25]; Z26 = out_3[26]; Z27 = out_3[27];
  //   Z28 = out_3[28]; Z29 = out_3[29]; Z30 = out_3[30]; Z31 = out_3[31]; Z32 = out_4[0]; Z33 = out_4[1];
  //   Z34 = out_4[2]; Z35 = out_4[3]; Z36 = out_4[4]; Z37 = out_4[5]; Z38 = out_4[6]; Z39 = out_4[7]; Z40 = out_4[8];
  //   Z41 = out_4[9]; Z42 = out_4[10]; Z43 = out_4[11]; Z44 = out_4[12]; Z45 = out_4[13]; Z46 = out_4[14];
  //   Z47 = out_4[15]; Z48 = out_4[16]; Z49 = out_4[17]; Z50 = out_4[18]; Z51 = out_4[19]; Z52 = out_4[20];
  //   Z53 = out_4[21]; Z54 = out_4[22]; Z55 = out_4[23]; Z56 = out_4[24]; Z57 = out_4[25]; Z58 = out_4[26];
  //   Z59 = out_4[27]; Z60 = out_4[28]; Z61 = out_4[29]; Z62 = out_4[30]; Z63 = out_4[31]
endmodule

module CELL (
  input  CIN,
  input  Ai,
  input  Bi,
  input  \部分积1位输入 ,
  output \部分积1位输出 ,
  output cout,
  output Bi_2,
  output Ai_2
);

  wire and_1_out;

  and and_1 (and_1_out, Ai, Bi);
  Adder #(.width(1)) adder_1 (.a(and_1_out), .b(\部分积1位输入 ), .out(\部分积1位输出 ), .cin(CIN), .cout(cout));

  assign Ai_2 = Ai;
  assign Bi_2 = Bi;
endmodule
