// Logisim project 思考题2.circ as structural Verilog: 1 circuit, main circuit main
module main (
  input  [31:0] in_1,
  input  [31:0] in_2,
  input  in_3,
  input  in_4,
  output [31:0] out_5,
  output [31:0] out_6
);

  wire LOAD, not_1_out, STOP;
  wire [7:0] counter_1_q;
  wire [31:0] adder32_1_s, multiplexer_1_out, multiplexer_2_out;
  wire [31:31] adder32_1_cout;

  Register #(.width(32), .Select("low")) register_1 (
    .D({adder32_1_cout[31], adder32_1_s[31:1]}), .en(not_1_out), .Q(out_5), .clk(in_4), .clr(in_3));
  not not_1 (not_1_out, STOP);
  Multiplexer #(.width(32), .enable("false")) multiplexer_1 (
    .in0({32{1'b0}}), .in1(in_1), .out(multiplexer_1_out), .sel(out_6[0]));
  Register #(.width(32), .Select("low")) register_2 (
    .D(multiplexer_2_out), .en(not_1_out), .Q(out_6), .clk(in_4), .clr(in_3));
  Adder32 adder32_1 (
    .Cin(1'b0), .Cout(adder32_1_cout[31]), .X(out_5), .Y(multiplexer_1_out), .S(adder32_1_s));  // open: OF, CF, ZF, SF
  Multiplexer #(.width(32), .enable("false")) multiplexer_2 (
    .in0({adder32_1_s[0], out_6[31:1]}), .in1(in_2), .out(multiplexer_2_out), .sel(LOAD));
  Counter #(.ongoal("stay")) counter_1 (
    .load(1'b0), .D({8{1'b0}}), .count(not_1_out), .Q(counter_1_q), .clk(in_4), .clr(in_3));  // open: carry, preset, down
  Comparator #(.mode("unsigned")) comparator_1 (.a(counter_1_q), .b(8'h21), .eq(STOP));  // open: gt, lt
  Comparator #(.mode("unsigned")) comparator_2 (.a(counter_1_q), .b({8{1'b0}}), .eq(LOAD));  // open: gt, lt

  // Other names for the same wires on the sheet: Z0[31:0] = out_6; clk = in_4; rst = in_3; X[31:0] = in_1;
  //   Y[31:0] = in_2; Z1[31:0] = out_5
endmodule
