// Logisim project lab5.2.circ as structural Verilog: 2 circuits, main circuit DataRam
// DataRAM
module DataRam (
  input  CLK,
  input  CLR,
  input  WE,
  input  [2:0] MemOp,
  input  [17:0] Addr,
  input  [31:0] Din,
  output AlignErr,
  output [31:0] DataOut
);

  wire and_1_out, and_2_out, and_3_out, and_4_out, or_1_out, or_2_out, or_3_out, or_4_out;
  wire [3:0] sel;
  wire [7:0] multiplexer_2_out, multiplexer_4_out, multiplexer_7_out, multiplexer_9_out, multiplexer_10_out;
  wire [15:0] multiplexer_3_out;
  wire [17:0] adder_1_out, adder_2_out, adder_3_out, adder_4_out, multiplexer_1_out, multiplexer_5_out,
       multiplexer_8_out;
  wire [31:0] bit_extender_1_out, bit_extender_2_out, bit_extender_3_out, bit_extender_4_out, result;

  Adder #(.width(18)) adder_1 (.a(Addr), .b(18'h3), .out(adder_1_out));  // open: cin, cout
  Adder #(.width(18)) adder_2 (.a(Addr), .b(18'h1), .out(adder_2_out));  // open: cin, cout
  Multiplexer #(.select(4), .width(18), .enable("false")) multiplexer_1 (
    .in8(Addr), .in12(adder_2_out), .in15(adder_1_out), .out(multiplexer_1_out), .sel(sel));  // open: in0, in1, in2, in3, in4, in5, in6, in7, in9, in10, in11, in13, in14
  Multiplexer #(.select(3), .width(8), .enable("false")) multiplexer_2 (
    .in0(Din[7:0]), .in4(Din[15:8]), .in7(Din[31:24]), .out(multiplexer_2_out), .sel(sel[2:0]));  // open: in1, in2, in3, in5, in6
  Multiplexer #(.select(4), .width(16), .enable("false")) multiplexer_3 (
    .in3(result[15:0]), .in12(result[31:16]), .out(multiplexer_3_out), .sel(sel));  // open: in0, in1, in2, in4, in5, in6, in7, in8, in9, in10, in11, in13, in14, in15
  sel_alignerr sel_alignerr_1 (
    .in_1(MemOp), .in_2(Addr), .sel3(sel[3]), .AlignErr(AlignErr), .sel2(sel[2]), .sel1(sel[1]), .sel0(sel[0]));
  and and_1 (and_1_out, sel[3], WE);
  Multiplexer #(.select(4), .width(8), .enable("false")) multiplexer_4 (
    .in1(result[7:0]), .in2(result[15:8]), .in4(result[23:16]), .in8(result[31:24]), .out(multiplexer_4_out),
    .sel(sel));  // open: in0, in3, in5, in6, in7, in9, in10, in11, in12, in13, in14, in15
  Adder #(.width(18)) adder_3 (.a(Addr), .b(18'h2), .out(adder_3_out));  // open: cin, cout
  or or_1 (or_1_out, sel[3], WE);
  assign bit_extender_1_out = {{24{1'b0}}, multiplexer_4_out};  // Bit_Extender bit_extender_1
  assign bit_extender_2_out = {{24{multiplexer_4_out[7]}}, multiplexer_4_out};  // Bit_Extender bit_extender_2
  assign bit_extender_3_out = {{16{1'b0}}, multiplexer_3_out};  // Bit_Extender bit_extender_3
  assign bit_extender_4_out = {{16{multiplexer_3_out[15]}}, multiplexer_3_out};  // Bit_Extender bit_extender_4
  Multiplexer #(.select(4), .width(18), .enable("false")) multiplexer_5 (
    .in4(Addr), .in12(Addr), .in15(adder_3_out), .out(multiplexer_5_out), .sel(sel));  // open: in0, in1, in2, in3, in5, in6, in7, in8, in9, in10, in11, in13, in14
  RAM #(.addrWidth(18), .bus("separate"), .Select("high"), .simpleMode("false")) ram_1 (
    .addr(multiplexer_1_out), .din(multiplexer_2_out), .data(result[31:24]), .str(and_1_out), .sel(or_1_out),
    .clk(CLK), .clr(CLR));  // open: ld
  Multiplexer #(.select(3), .width(32), .enable("false")) multiplexer_6 (
    .in0(result), .in1(bit_extender_1_out), .in2(bit_extender_3_out), .in5(bit_extender_2_out),
    .in6(bit_extender_4_out), .out(DataOut), .sel(MemOp));  // open: in3, in4, in7
  Multiplexer #(.select(3), .width(8), .enable("false")) multiplexer_7 (
    .in0(Din[7:0]), .in4(Din[7:0]), .in7(Din[23:16]), .out(multiplexer_7_out), .sel({sel[3], sel[1:0]}));  // open: in1, in2, in3, in5, in6
  Adder #(.width(18)) adder_4 (.a(Addr), .b(18'h1), .out(adder_4_out));  // open: cin, cout
  and and_2 (and_2_out, sel[2], WE);
  Multiplexer #(.select(4), .width(18), .enable("false")) multiplexer_8 (
    .in2(Addr), .in3(adder_4_out), .in15(adder_4_out), .out(multiplexer_8_out), .sel(sel));  // open: in0, in1, in4, in5, in6, in7, in8, in9, in10, in11, in12, in13, in14
  RAM #(.addrWidth(18), .bus("separate"), .Select("high"), .simpleMode("false")) ram_2 (
    .addr(multiplexer_5_out), .din(multiplexer_7_out), .data(result[23:16]), .str(and_2_out), .sel(or_2_out),
    .clk(CLK), .clr(CLR));  // open: ld
  or or_2 (or_2_out, sel[2], WE);
  Multiplexer #(.select(3), .width(8), .enable("false")) multiplexer_9 (
    .in0(Din[7:0]), .in1(Din[15:8]), .in7(Din[15:8]), .out(multiplexer_9_out), .sel({sel[3:2], sel[0]}));  // open: in2, in3, in4, in5, in6
  and and_3 (and_3_out, sel[1], WE);
  RAM #(.addrWidth(18), .bus("separate"), .Select("high"), .simpleMode("false")) ram_3 (
    .addr(multiplexer_8_out), .din(multiplexer_9_out), .data(result[15:8]), .str(and_3_out), .sel(or_3_out),
    .clk(CLK), .clr(CLR));  // open: ld
  or or_3 (or_3_out, sel[1], WE);
  Multiplexer #(.select(3), .width(8), .enable("false")) multiplexer_10 (
    .in0(Din[7:0]), .in1(Din[7:0]), .in7(Din[7:0]), .out(multiplexer_10_out), .sel(sel[3:1]));  // open: in2, in3, in4, in5, in6
  and and_4 (and_4_out, sel[0], WE);
  RAM #(.addrWidth(18), .bus("separate"), .Select("high"), .simpleMode("false")) ram_4 (
    .addr(Addr), .din(multiplexer_10_out), .data(result[7:0]), .str(and_4_out), .sel(or_4_out), .clk(CLK),
    .clr(CLR));  // open: ld
  or or_4 (or_4_out, sel[0], WE);

  // Other names for the same wires on the sheet: Dout[31:0] = DataOut

  // Notes on the sheet:
  //   输入引脚
  //   请勿修改引脚名称、电路名称及电路封装外观
  //   为了后续实验中的引用，不要修改MemOp的编码定义、引脚名称和在布局中的位置。
  //   32位数据存储器，按字节分4片存储，可按照字节、半字和字进行存储；读取字节或半字时，支持0扩展和符号位扩展。
  //   SEL3
  //   输出引脚
  //   SEL2
  //   SEL1
  //   SEL0
endmodule

module sel_alignerr (
  input  [2:0] in_1,
  input  [17:0] in_2,
  output sel3,
  output AlignErr,
  output sel2,
  output sel1,
  output sel0
);

  wire and_1_out, and_2_out, and_3_out, and_4_out, and_5_out, and_6_out, and_7_out;

  and and_1 (and_1_out, ~in_1[2], ~in_1[1], ~in_1[0], ~in_2[1], ~in_2[0]);  // AND_Gate
  and and_2 (and_2_out, ~in_1[1], in_1[0], in_2[1], in_2[0]);  // AND_Gate
  and and_3 (and_3_out, in_1[1], ~in_1[0], in_2[1], ~in_2[0]);  // AND_Gate
  and and_4 (and_4_out, ~in_1[1], in_1[0], in_2[1], ~in_2[0]);  // AND_Gate
  and and_5 (and_5_out, ~in_1[1], in_1[0], ~in_2[1], in_2[0]);  // AND_Gate
  and and_6 (and_6_out, in_1[1], ~in_1[0], ~in_2[1], ~in_2[0]);  // AND_Gate
  and and_7 (and_7_out, ~in_1[1], in_1[0], ~in_2[1], ~in_2[0]);  // AND_Gate
  or or_1 (sel3, and_1_out, and_2_out, and_3_out);
  or or_2 (sel2, and_1_out, and_3_out, and_4_out);
  or or_3 (sel1, and_1_out, and_5_out, and_6_out);
  or or_4 (sel0, and_1_out, and_7_out, and_6_out);
  and and_8 (AlignErr, ~sel3, ~sel2, ~sel1, ~sel0);  // AND_Gate

  // Other names for the same wires on the sheet: Addr[17:0] = in_2; MemOp[2:0] = in_1
endmodule
