// Logisim project 思考题（左右）.circ as structural Verilog: 1 circuit, main circuit main
module main (
  input  [6:0] in_1,
  input  [6:0] in_2,
  input  [6:0] in_3,
  input  [6:0] in_4,
  input  [6:0] in_5,
  input  in_6,
  input  in_7
);

  wire [2:0] counter_1_q;
  wire [6:0] multiplexer_1_out, multiplexer_2_out, multiplexer_3_out;
  wire [7:0] _0, _1, _2, _3, _4, _5, _6, _7, _8, _9, _10, _11, _12, _13, _14, _15, _20, _21, _22, _23, _24,
       _25, _26, _27, _28, _29, _30, _31, _32, _33, _34, _35, main_1_row1, main_1_row2, main_1_row3,
       main_1_row4, main_1_row5, main_1_row6, main_1_row7, main_1_row8, main_1_row9, main_1_row10,
       main_1_row11, main_1_row12, main_1_row13, main_1_row14, main_1_row15, main_1_row16;

  Counter #(.width(3), .max('h4)) counter_1 (
    .Q(counter_1_q), .clk(in_6), .down(in_7));  // open: load, D, count, carry, clr, preset
  Multiplexer #(.select(3), .width(7), .enable("false")) multiplexer_1 (
    .in0(in_1), .in1(in_2), .in2(in_3), .in3(in_4), .in4(in_5), .out(multiplexer_1_out), .sel(counter_1_q));  // open: in5, in6, in7
  Multiplexer #(.select(3), .width(7), .enable("false")) multiplexer_2 (
    .in0(in_2), .in1(in_3), .in2(in_4), .in3(in_5), .in4(in_1), .out(multiplexer_2_out), .sel(counter_1_q));  // open: in5, in6, in7
  Multiplexer #(.select(3), .width(7), .enable("false")) multiplexer_3 (
    .in0(in_3), .in1(in_4), .in2(in_5), .in3(in_1), .in4(in_2), .out(multiplexer_3_out), .sel(counter_1_q));  // open: in5, in6, in7
  lab5_1_main main_1 (
    .ASCII_CODE(multiplexer_1_out), .row1(main_1_row1), .row2(main_1_row2), .row3(main_1_row3),
    .row4(main_1_row4), .row7(main_1_row7), .row5(main_1_row5), .row6(main_1_row6), .row8(main_1_row8),
    .row9(main_1_row9), .row10(main_1_row10), .row11(main_1_row11), .row12(main_1_row12),
    .row13(main_1_row13), .row14(main_1_row14), .row15(main_1_row15), .row16(main_1_row16));  // open: CodeErr
  lab5_1_main main_2 (
    .ASCII_CODE(multiplexer_2_out), .row1(_0), .row2(_1), .row3(_2), .row4(_3), .row7(_6), .row5(_4),
    .row6(_5), .row8(_7), .row9(_8), .row10(_9), .row11(_10), .row12(_11), .row13(_12), .row14(_13),
    .row15(_14), .row16(_15));  // open: CodeErr
  lab5_1_main main_3 (
    .ASCII_CODE(multiplexer_3_out), .row1(_20), .row2(_21), .row3(_22), .row4(_23), .row7(_26), .row5(_24),
    .row6(_25), .row8(_27), .row9(_28), .row10(_29), .row11(_30), .row12(_31), .row13(_32), .row14(_33),
    .row15(_34), .row16(_35));  // open: CodeErr
  DotMatrix #(.inputtype("row"), .matrixcols(8), .matrixrows(16)) dotmatrix_1 (
    .row0(main_1_row1), .row1(main_1_row2), .row2(main_1_row3), .row3(main_1_row4), .row4(main_1_row5),
    .row5(main_1_row6), .row6(main_1_row7), .row7(main_1_row8), .row8(main_1_row9), .row9(main_1_row10),
    .row10(main_1_row11), .row11(main_1_row12), .row12(main_1_row13), .row13(main_1_row14),
    .row14(main_1_row15), .row15(main_1_row16));
  DotMatrix #(.inputtype("row"), .matrixcols(8), .matrixrows(16)) dotmatrix_2 (
    .row0(_0), .row1(_1), .row2(_2), .row3(_3), .row4(_4), .row5(_5), .row6(_6), .row7(_7), .row8(_8),
    .row9(_9), .row10(_10), .row11(_11), .row12(_12), .row13(_13), .row14(_14), .row15(_15));
  DotMatrix #(.inputtype("row"), .matrixcols(8), .matrixrows(16)) dotmatrix_3 (
    .row0(_20), .row1(_21), .row2(_22), .row3(_23), .row4(_24), .row5(_25), .row6(_26), .row7(_27),
    .row8(_28), .row9(_29), .row10(_30), .row11(_31), .row12(_32), .row13(_33), .row14(_34), .row15(_35));

  // Other names for the same wires on the sheet: Clk = in_6; En = in_7
endmodule
