// Logisim project lab6.1.circ as structural Verilog: 1 circuit, main circuit 控制器
module \控制器  (
  input  [6:0] opcode,
  input  [2:0] funct3,
  input  [6:0] funct7,
  output [2:0] ExtOp,
  output RegWr,
  output [2:0] BandJ,
  output ALUASrc,
  output [1:0] ALUBSrc,
  output [3:0] ALUctr,
  output MemtoReg,
  output [2:0] MemOp,
  output MemWr
);

  wire and_1_out, and_2_out, and_3_out, and_4_out, and_5_out, and_6_out, and_7_out, and_8_out, and_9_out,
       and_10_out, and_11_out, and_12_out, and_13_out, and_14_out, and_15_out, and_16_out, and_17_out,
       I_Arith, I_jalr, R_Arith, U_auipc, U_lui;

  Comparator #(.width(7), .mode("unsigned")) comparator_1 (.a(opcode), .b(7'b0110111), .eq(U_lui));  // open: gt, lt
  Comparator #(.width(7), .mode("unsigned")) comparator_2 (.a(opcode), .b(7'b1100111), .eq(I_jalr));  // open: gt, lt
  Comparator #(.width(7), .mode("unsigned")) comparator_3 (.a(opcode), .b(7'b0010111), .eq(U_auipc));  // open: gt, lt
  Comparator #(.width(7), .mode("unsigned")) comparator_4 (.a(opcode), .b(7'b1100011), .eq(BandJ[2]));  // open: gt, lt
  Comparator #(.width(7), .mode("unsigned")) comparator_5 (.a(opcode), .b(7'b0010011), .eq(I_Arith));  // open: gt, lt
  Comparator #(.width(7), .mode("unsigned")) comparator_6 (.a(opcode), .b(7'b0000011), .eq(MemtoReg));  // open: gt, lt
  Comparator #(.width(7), .mode("unsigned")) comparator_7 (.a(opcode), .b(7'b0110011), .eq(R_Arith));  // open: gt, lt
  Comparator #(.width(7), .mode("unsigned")) comparator_8 (.a(opcode), .b(7'b0100011), .eq(MemWr));  // open: gt, lt
  or or_1 (RegWr, U_lui, U_auipc, I_Arith, R_Arith, ExtOp[2], I_jalr, MemtoReg);
  or or_2 (ALUASrc, U_auipc, ExtOp[2], I_jalr);
  or or_3 (ALUBSrc[1], U_lui, U_auipc, I_Arith, MemtoReg, MemWr);
  or or_4 (ALUBSrc[0], ExtOp[2], I_jalr);
  or or_5 (ExtOp[0], U_lui, U_auipc, BandJ[2]);
  or or_6 (ExtOp[1], BandJ[2], MemWr);
  and and_1 (and_1_out, I_Arith, funct3[0]);
  or or_7 (ALUctr[0], U_lui, and_1_out, and_2_out, and_3_out);
  and and_2 (and_2_out, R_Arith, funct3[0]);
  and and_3 (and_3_out, BandJ[2], funct3[1], funct3[2]);
  and and_4 (and_4_out, I_Arith, funct3[1]);
  or or_8 (ALUctr[1], U_lui, and_4_out, and_5_out, BandJ[2]);
  and and_5 (and_5_out, R_Arith, funct3[1]);
  and and_6 (and_6_out, I_Arith, funct3[2]);
  or or_9 (ALUctr[2], U_lui, and_6_out, and_7_out);
  and and_7 (and_7_out, R_Arith, funct3[2]);
  and and_8 (and_8_out, funct7[5], I_Arith, funct3[0], ~funct3[1], funct3[2]);  // AND_Gate
  or or_10 (ALUctr[3], U_lui, and_8_out, and_9_out);
  and and_9 (and_9_out, R_Arith, funct7[5]);
  or or_11 (BandJ[0], ExtOp[2], and_10_out);
  and and_10 (and_10_out, BandJ[2], funct3[0]);
  or or_12 (BandJ[1], I_jalr, and_11_out);
  and and_11 (and_11_out, BandJ[2], funct3[2]);
  and and_12 (and_12_out, MemtoReg, ~funct3[0], ~funct3[1]);  // AND_Gate
  or or_13 (MemOp[0], and_12_out, and_13_out);
  and and_13 (and_13_out, MemWr, ~funct3[0], ~funct3[1]);  // AND_Gate
  and and_14 (and_14_out, MemtoReg, funct3[0], ~funct3[1]);  // AND_Gate
  or or_14 (MemOp[1], and_14_out, and_15_out);
  and and_15 (and_15_out, MemWr, funct3[0], ~funct3[1]);  // AND_Gate
  and and_16 (and_16_out, MemtoReg, ~funct3[1], ~funct3[2]);  // AND_Gate
  or or_15 (MemOp[2], and_16_out, and_17_out);
  and and_17 (and_17_out, MemWr, ~funct3[1], ~funct3[2]);  // AND_Gate
  Comparator #(.width(7), .mode("unsigned")) comparator_9 (.a(opcode), .b(7'b1101111), .eq(ExtOp[2]));  // open: gt, lt

  // Other names for the same wires on the sheet: B_Instr = BandJ[2]; J_jal = ExtOp[2]; I_load = MemtoReg;
  //   S_Instr = MemWr

  // Notes on the sheet:
  //   输入引脚
  //   请勿修改引脚名称、电路名称及电路封装外观
  //   提示：根据指令种类，把7位指令code用一位指令类型标志位来表示，再通过功能码来区分具体指令，生成控制信号。
  //   输出引脚
endmodule
